# Fritzing sketch Remote2_Fritzing (saved by Fritzing 0.7.10b)
breadboards: 1

parts:
  Arduino1 = Arduino
  Q1 = NPN-Transistor [package="TO92 [THT]"]
  S1 = Pushbutton [package="[THT]"]
  S2 = Pushbutton [package="[THT]"]
  S3 = Pushbutton [package="[THT]"]
  LED1 = LED - 5mm [color="Red (633nm)" package="5 mm [THT]"]
  R1 = Resistor [tolerance=±5% resistance=1k package=THT]
  LED2 = LED - 5mm [color="Infrared (940nm)" package="5 mm [THT]"]
  R2 = Resistor [tolerance=±5% resistance=68 package=THT]
  R3 = Resistor [tolerance=±5% resistance=220 package=THT]
  R4 = Resistor [tolerance=±5% resistance=22k package=THT]
  R5 = Resistor [tolerance=±5% resistance=15k package=THT]
  R6 = Resistor [tolerance=±5% resistance=10k package=THT]
  R7 = Resistor [tolerance=±5% resistance=100k package=THT]
  VCC1 = Battery block 9V

nets:
  N1: Arduino1.GND, Q1.E, R3.Pin_0, R7.Pin_0, VCC1.-
  N2: Arduino1.D11, LED1.anode
  N3: Arduino1.D3, R1.Pin_0
  N4: Arduino1.+5V, R2.Pin_1
  N5: Arduino1.VIN, VCC1.+
  N6: Arduino1.A0, S1.Pin_3, S1.Pin_4, S2.Pin_3, S2.Pin_4, S3.Pin_3, S3.Pin_4, R7.Pin_1
  N7: Q1.B, R1.Pin_1
  N8: Q1.C, LED2.cathode
  N9: S1.Pin_1, S1.Pin_2, R6.Pin_0
  N10: S2.Pin_1, S2.Pin_2, R5.Pin_0
  N11: S3.Pin_1, S3.Pin_2, R4.Pin_0
  N12: LED1.cathode, R3.Pin_1
  N13: LED2.anode, R2.Pin_0
  N14: R4.Pin_1, R5.Pin_1, R6.Pin_1
